# Fritzing sketch Thermostat (saved by Fritzing 0.8.7b)

parts:
  Part1 = OLED Monochrome 128x64 0.96 inch [part_number=326]
  KY-1 = Keyes Relay [package=THT]
  R1 = Trimmer Potentiometer [maximum_resistance=10kΩ package=THT]  # not connected
  U2 = POT [package=pot_alpha_rv16af-20]
  Raspberry_Pi1 = Raspberry Pi Zero
  DHT1 = DHT22 Humidity and Temperature Sensor
  R2 = Resistor [tolerance=±5% resistance=10k package=THT]  # not connected

nets:
  N1: Part1.MOSI_SDA, Raspberry_Pi1.GPIO2
  N2: Part1.SCLK_SCK, Raspberry_Pi1.GPIO3
  N3: Part1.RESET, Raspberry_Pi1.GIPO4
  3V3: Part1.VIN, U2.E, Raspberry_Pi1.3v3, Raspberry_Pi1.3V3
  N4: Part1.GND, Raspberry_Pi1.GIPO18
  N5: KY-1.signal, Raspberry_Pi1.GIPO17
  5V: KY-1.power, Raspberry_Pi1.5V, DHT1.VDD
  N6: KY-1.ground, U2.A, Raspberry_Pi1.GND
  N7: U2.S, Raspberry_Pi1.GIPO27
  N8: Raspberry_Pi1.GIPO22, DHT1.DATA

notes:
  REMOVE R1 AND WIRE IN TRIMMER
  REMOVE R1 FROM RELAY

custom parts:
  OLED Monochrome 128x64 0.96 inch: These displays are small, only about 1" diameter, but very readable due to the high contrast of an OLED display. This display is made of 128x64 individual white OLED pixels, each one is turned on or off by the controller chip. Because the display makes its own light, no backlight is required. This reduces the power required to run the OLED and is why the display has such high contrast; we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
  Keyes Relay: The Keyes 5V relay module is suitable for SCM development, home appliance control. It uses a 5V~12V TIL control signal which can control DC / AC signal.
  Raspberry Pi Zero: The Raspberry Pi Zero is the latest single board computer to be released by the Raspberry Pi Foundation. It is the entry level model Raspberry Pi perfect for hobbyists, makers and industrial engineers looking to create solutions where small size and low power consumption are important. This is especially relevant for applications in the wearables space as well as up and coming applications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
